# Fritzing sketch Anschlussplan DRV8833 mit Encoder-Servo 03 (saved by Fritzing 1.0.4)
breadboards: 1

parts:
  4_7_kOhm = Resistor [package=THT]
  Bauteil2 = Adafruit DRV8833 DC/Stepper Motor Driver [part_number="Adafruit #3297"]
  M2 = Dagu DGServo 9g (Top view) [part_number=RS001B]

nets:
  N1: 4_7_kOhm.Pin_0, Bauteil2.!SLEEP, M2.vcc
  GND: Bauteil2.GND, M2.gnd

custom parts:
  Resistor: A generic 5-band resistor (0.25W)
  Adafruit DRV8833 DC/Stepper Motor Driver: Spin two DC motors or step one bi-polar or uni-polar stepper with up to 1.2A per channel using the DRV8833. This motor driver chip is a nice alternative to the TB6612 driver. Like that chip, you get 2 full H-bridges, but this chip is better for low voltage uses (can run from 2.7V up to 10.8V motor power) and has built in current limiting capability. We set it up for 1A current limiting so you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
